// Logisim project parcialFinal.circ as structural Verilog: 7 circuits, main circuit main
module main (
);

  wire clock_1_out, comparator_1_eq, comparator_1_gt, comparator_1_lt, detectordecambios_1_out_5,
       dipswitch_1_p1, dipswitch_1_p3, dipswitch_1_p4, dipswitch_1_p5, dipswitch_2_p1, dipswitch_2_p2,
       dipswitch_2_p3, iszero_1_out_2, multiplexer_1_out;
  wire [1:0] memoria2bits_1_out_3, memoria2bits_2_out_3, sumadordeactivos_1_out_4, sumadordeactivos_2_out_4;
  wire [3:0] counter_1_q, displayhandler_1_out_2, displayhandler_1_out_3, subtractor_1_out;

  Hex_Digit_Display hex_digit_display_1 (.value({2'b00, sumadordeactivos_1_out_4}));  // open: dp
  Hex_Digit_Display hex_digit_display_2 (.value({2'b00, sumadordeactivos_2_out_4}));  // open: dp
  Multiplexer #(.enable("false")) multiplexer_1 (
    .in1(clock_1_out), .out(multiplexer_1_out), .sel(detectordecambios_1_out_5));  // open: in0
  // DipSwitch #(.NSwitches(3)) dipswitch_1: pin names not known; wires that end beside it: dipswitch_1_p1, dipswitch_1_p1, dipswitch_1_p3, dipswitch_1_p4, dipswitch_1_p5
  // DipSwitch #(.NSwitches(3)) dipswitch_2: pin names not known; wires that end beside it: dipswitch_2_p1, dipswitch_2_p2, dipswitch_2_p3
  Counter #(.width(4), .max('hf)) counter_1 (
    .Q(counter_1_q), .clk(multiplexer_1_out));  // open: load, D, count, carry, clr, preset, down
  Clock clock_1 (.out(clock_1_out));
  SumadorDeActivos sumadordeactivos_1 (
    .in_1(dipswitch_1_p3), .in_2(dipswitch_1_p4), .in_3(dipswitch_1_p5), .out_4(sumadordeactivos_1_out_4));
  SumadorDeActivos sumadordeactivos_2 (
    .in_1(dipswitch_2_p1), .in_2(dipswitch_2_p2), .in_3(dipswitch_2_p3), .out_4(sumadordeactivos_2_out_4));
  Subtractor #(.width(4)) subtractor_1 (.a(4'b1111), .b(counter_1_q), .out(subtractor_1_out));  // open: bin, bout
  displayHandler displayhandler_1 (
    .in_1(subtractor_1_out), .out_2(displayhandler_1_out_2), .out_3(displayhandler_1_out_3));
  IsZero iszero_1 (.in_1(subtractor_1_out), .out_2(iszero_1_out_2));
  Hex_Digit_Display hex_digit_display_3 (.value(displayhandler_1_out_2));  // open: dp
  Hex_Digit_Display hex_digit_display_4 (.value(displayhandler_1_out_3));  // open: dp
  memoria2bits memoria2bits_1 (
    .PULSO_DE_CAMBIO(iszero_1_out_2), .A(sumadordeactivos_1_out_4), .out_3(memoria2bits_1_out_3));
  detectorDeCambios detectordecambios_1 (
    .N(sumadordeactivos_1_out_4), .A(memoria2bits_1_out_3), .N_2(sumadordeactivos_2_out_4),
    .A_2(memoria2bits_2_out_3), .out_5(detectordecambios_1_out_5));
  memoria2bits memoria2bits_2 (
    .PULSO_DE_CAMBIO(iszero_1_out_2), .A(sumadordeactivos_2_out_4), .out_3(memoria2bits_2_out_3));
  Comparator #(.width(2), .mode("unsigned")) comparator_1 (
    .a(memoria2bits_1_out_3), .b(memoria2bits_2_out_3), .gt(comparator_1_gt), .eq(comparator_1_eq),
    .lt(comparator_1_lt));
  // RGBLed rgbled_1: pin names not known; wires that end beside it: sumadordeactivos_1_out_4, memoria2bits_1_out_3, sumadordeactivos_2_out_4, memoria2bits_2_out_3, comparator_1_lt
  // RGBLed rgbled_2: pin names not known; wires that end beside it: comparator_1_eq, comparator_1_eq
  // RGBLed rgbled_3: pin names not known; wires that end beside it: comparator_1_gt

  // Notes on the sheet:
  //   REACTORES
  //   ENFRIAMIENTO
  //   SUMADORDEACTIVOS
  //   CUENTAREGRESIVA
  //   DisplayHandler
  //   Guardado De Datos
  //   SALIDA
endmodule

module SumadorDeActivos (
  input  in_1,
  input  in_2,
  input  in_3,
  output [1:0] out_4
);

  wire [1:0] adder_1_out;

  Adder #(.width(1)) adder_1 (.a(in_2), .b(in_3), .out(adder_1_out[0]), .cout(adder_1_out[1]));  // open: cin
  Adder #(.width(2)) adder_2 (.a({1'b0, in_1}), .b(adder_1_out), .out(out_4));  // open: cin, cout
endmodule

module memoria2bits (
  input  PULSO_DE_CAMBIO,
  input  [1:0] A,
  output [1:0] out_3
);

  D_Flip_Flop d_ff_1 (.clk(PULSO_DE_CAMBIO), .D(A[0]), .Q(out_3[0]));  // open: Qn, preset, reset
  D_Flip_Flop d_ff_2 (.clk(PULSO_DE_CAMBIO), .D(A[1]), .Q(out_3[1]));  // open: Qn, preset, reset

  // Notes on the sheet:
  //   A_{(2)}
endmodule

module IsZero (
  input  [3:0] in_1,
  output out_2
);

  Comparator #(.width(4)) comparator_1 (.a(4'b0000), .b(in_1), .eq(out_2));  // open: gt, lt
endmodule

module ISorISNotEqual (
  input  [1:0] in_1,
  input  [1:0] in_2,
  output out_3
);

  wire comparator_1_gt, comparator_1_lt, or_1_out;

  Comparator #(.width(2)) comparator_1 (.a(in_1), .b(in_2), .gt(comparator_1_gt), .lt(comparator_1_lt));  // open: eq
  not not_1 (out_3, or_1_out);
  or or_1 (or_1_out, comparator_1_gt, comparator_1_lt);
endmodule

module detectorDeCambios (
  input  [1:0] N,
  input  [1:0] A,
  input  [1:0] N_2,
  input  [1:0] A_2,
  output out_5
);

  wire isorisnotequal_1_out_3, isorisnotequal_2_out_3, not_1_out, not_2_out;

  ISorISNotEqual isorisnotequal_1 (.in_1(N), .in_2(A), .out_3(isorisnotequal_1_out_3));
  ISorISNotEqual isorisnotequal_2 (.in_1(N_2), .in_2(A_2), .out_3(isorisnotequal_2_out_3));
  not not_1 (not_1_out, isorisnotequal_1_out_3);
  not not_2 (not_2_out, isorisnotequal_2_out_3);
  or or_1 (out_5, not_1_out, not_2_out);

  // Notes on the sheet:
  //   N : NUEVO DATO
  //   A: ANTIGUO DATO
  //   REACTORES
  //   ENFRIADORES
endmodule

module displayHandler (
  input  [3:0] in_1,
  output [3:0] out_2,
  output [3:0] out_3
);

  wire comparator_1_lt;

  Comparator #(.width(4), .mode("unsigned")) comparator_1 (
    .a(in_1), .b(4'b1010), .lt(comparator_1_lt));  // open: gt, eq
  Divider #(.width(4)) divider_1 (.a(in_1), .b(4'b1010), .rem(out_3));  // open: out, upper
  Multiplexer #(.width(4), .enable("false")) multiplexer_1 (
    .in0(4'b0001), .in1(4'b0000), .out(out_2), .sel(comparator_1_lt));
endmodule
